# Fritzing sketch stepper_drivers_xiao_esp32c3 (saved by Fritzing 1.0.0)

parts:
  U1 = Seeed XIAO ESP32C3
  DRV1 = ULN2003 Stepper Driver Board (right header)
  DRV2 = ULN2003 Stepper Driver Board (right header)
  DRV3 = ULN2003 Stepper Driver Board (left header)
  PS1 = 5V DC Supply (1A+)

nets:
  N1: U1.D0, DRV1.IN1
  N2: U1.D1, DRV1.IN2
  N3: U1.D2, DRV1.IN3
  N4: U1.D3, DRV1.IN4
  N5: U1.D4, DRV2.IN1
  N6: U1.D5, DRV2.IN2
  N7: U1.D6, DRV2.IN3
  GND: U1.GND, DRV1.GND_(-), DRV2.GND_(-), DRV3.GND_(-), PS1.GND
  N8: U1.D10, DRV3.IN1
  N9: U1.D9, DRV3.IN2
  N10: U1.D8, DRV3.IN3
  N11: U1.D7, DRV3.IN4
  N12: DRV1.V+_(5-12V), DRV2.V+_(5-12V), DRV3.V+_(5-12V), PS1.V+_(5V)

custom parts:
  Seeed XIAO ESP32C3: Seeed Studio XIAO ESP32C3 (custom part). USB-C at top. Left: D0-D6, right: 5V GND 3V3 D10-D7.
  ULN2003 Stepper Driver Board (right header): ULN2003 + 28BYJ-48 stepper driver board with 5-pin motor socket (custom part).
  ULN2003 Stepper Driver Board (left header): ULN2003 + 28BYJ-48 stepper driver board with 5-pin motor socket (custom part).
  5V DC Supply (1A+): Generic external 5 V supply (custom part).
